# Fritzing sketch AquqriumEnvMngSys (saved by Fritzing 0.9.10b)
breadboards: 1

parts:
  Raspberry_Pi_1 = Raspberry Pi 3 [part_number=RPI-3-V1.2]
  DS1 = DS18B20 1-Wire Temperature Sensor Probe
  パーツ1 = LCD1602-I2C
  R1 = Resistor [tolerance=±5% power=0.25 resistance=4.7k package=THT]
  SHT35-D1 = SHT35-D [package="SIP (Single Inline) [THT]"]

nets:
  3V3: Raspberry_Pi_1.3v3, DS1.VDD, パーツ1.VCC, R1.Pin_1
  N1: Raspberry_Pi_1.GPIO2, パーツ1.SDA, SHT35-D1.SDA
  N2: Raspberry_Pi_1.GPIO3, パーツ1.SCL, SHT35-D1.SCL
  N3: Raspberry_Pi_1.GPIO4, DS1.DQ, R1.Pin_0
  GND: Raspberry_Pi_1.GND, DS1.GND, パーツ1.GND

notes:
  I2C SCL（Pin5）
  I2C SDA（Pin３）
  temperature and humidity sensor
  （I2C）
  DS18B20
  防水温度センサ
  (1Wire)
  [ACM1602NI-FLW-FBW-M01]
  (I2C)
  [1WIRE 通信]
  GPIO4（Pin7）
  3.3V
  [GND]
  4.7kΩ

custom parts:
  LCD1602-I2C: A standard character display, usually with 2x16 characters. Comes in many colors with LCM1602 IIC attached.
  SHT35-D: SHT35-D is an I2C connected temperature and humidity sensor
