# Fritzing sketch PrjAquaEnvMngSysLite (saved by Fritzing 0.9.10b)
breadboards: 1

parts:
  DS2 = DS18B20 1-Wire Temperature Sensor Probe
  パーツ2 = LCD1602-I2C
  R2 = Resistor [tolerance=±5% power=0.25 resistance=4.7k package=THT]
  Mod1 = Raspberry Pi Pico

nets:
  GND: DS2.GND, パーツ2.GND, Mod1.pin_3, Mod1.pin_8, Mod1.pin_13, Mod1.pin_18, Mod1.pin_23, Mod1.pin_28, Mod1.pin_33, Mod1.pin_38, Mod1.pin_42
  N1: DS2.DQ, R2.Pin_0, Mod1.pin_6
  VDD: DS2.VDD, パーツ2.VCC, R2.Pin_1, Mod1.pin_36
  N2: パーツ2.SDA, Mod1.pin_4
  N3: パーツ2.SCL, Mod1.pin_5

notes:
  4.7kΩ
  I2C1 SDA（Pin4）
  DS18B20
  防水温度センサ
  (1Wire)
  [ACM1602NI-FLW-FBW-M01]
  I2C1 SCL(Pin5)
  [1WIRE 通信]
  GPIO4（Pin6）
  3.3V
  [GND]

custom parts:
  LCD1602-I2C: A standard character display, usually with 2x16 characters. Comes in many colors with LCM1602 IIC attached.
  Raspberry Pi Pico: Raspberry Pi Pico. Based around the RP2040 microcontroller the Pico is a low cost microcontroller device bringing Raspberry Pi quality, cost, and easy of use to the microcontroller space. Jan 2021, Split part in to two versions: tht (this one) and SMD. This one will drill holes for a .1 in header in pcb to allow plugging in the module as well as providing pads to solder the module to the top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
